# Fritzing sketch PuzzleBox (saved by Fritzing 0.9.3b)
breadboards: 1

parts:
  Part1 = Arduino Pro Mini v13
  LED_1 = LEDs [package=led10mm]
  LED_0 = LEDs [package=led10mm]
  LED_2 = LEDs [package=led10mm]
  LED_3 = LEDs [package=led10mm]
  LED_4 = LEDs [package=led10mm]
  VCC1 = 4 x AAA Battery Mount
  Reed_Switch_4 = Reed switch [package=THT]
  Reed_Switch_3 = Reed switch [package=THT]
  Reed_Switch_2 = Reed switch [package=THT]
  Reed_Switch_0 = Reed switch [package=THT]
  Reed_Switch_1 = Reed switch [package=THT]
  Plug_0 = BNC [package=bnc]
  Plug_1 = BNC [package=bnc]
  Plug_2 = BNC [package=bnc]
  Plug_3 = BNC [package=bnc]
  Plug_4 = BNC [package=bnc]
  Plug_5 = BNC [package=bnc]
  Plug_6 = BNC [package=bnc]
  Plug_7 = BNC [package=bnc]
  Plug_8 = BNC [package=bnc]
  Plug_9 = BNC [package=bnc]
  R6 = Resistor [tolerance=±5% resistance=220 package=THT]
  R7 = Resistor [tolerance=±5% resistance=220 package=THT]
  R8 = Resistor [tolerance=±5% resistance=220 package=THT]
  R9 = Resistor [tolerance=±5% resistance=220 package=THT]
  R10 = Resistor [tolerance=±5% resistance=220 package=THT]
  R11 = Resistor [tolerance=±5% resistance=220 package=THT]
  LED_5 = LEDs [package=led10mm]
  Front_Drawer = Basic Servo
  Right_Drawer = Basic Servo
  J1 = Dagu DGServo 9g header connector (female) [package=THT]
  J2 = Dagu DGServo 9g header connector (female) [package=THT]

nets:
  GND: Part1.GND, LED_1.A, LED_0.A, LED_2.A, LED_3.A, LED_4.A, VCC1.-, Plug_0.GND, Plug_1.GND, Plug_2.GND, Plug_3.GND, Plug_4.GND, Plug_5.GND, Plug_6.GND, Plug_7.GND, Plug_8.GND, Plug_9.GND, LED_5.A, Front_Drawer.gnd, Right_Drawer.gnd, J1.gnd, J2.gnd
  N1: Part1.A4, R8.Pin_0
  N2: Part1.A5, R6.Pin_0
  N3: Part1.RAW, Reed_Switch_4.pin_1
  VCC: Part1.VCC, Front_Drawer.vcc, Right_Drawer.vcc, J1.Vcc, J2.Vcc
  N4: Part1.A3, R7.Pin_0
  N5: Part1.A2, R9.Pin_0
  N6: Part1.A1, R10.Pin_0
  N7: Part1.A0, R11.Pin_0
  N8: Part1.D11_PWM/MOSI, Front_Drawer.pulse, J1.pulse
  N9: Part1.D10_PWM/SS, Right_Drawer.pulse, J2.pulse
  N10: Part1.D9_PWM, Plug_9.OUT
  N11: Part1.D8, Plug_8.OUT
  N12: Part1.D7, Plug_7.OUT
  N13: Part1.D6_PWM, Plug_6.OUT
  N14: Part1.D5_PWM, Plug_5.OUT
  N15: Part1.D4, Plug_4.OUT
  N16: Part1.D3_PWM, Plug_3.OUT
  N17: Part1.D2, Plug_2.OUT
  N18: Part1.D1/RX, Plug_1.OUT
  N19: Part1.D0/TX, Plug_0.OUT
  N20: LED_1.C, R10.Pin_1
  N21: LED_0.C, R11.Pin_1
  N22: LED_2.C, R9.Pin_1
  N23: LED_3.C, R8.Pin_1
  N24: LED_4.C, R7.Pin_1
  N25: VCC1.+, Reed_Switch_0.pin_2
  N26: Reed_Switch_4.pin_2, Reed_Switch_3.pin_1
  N27: Reed_Switch_3.pin_2, Reed_Switch_2.pin_1
  N28: Reed_Switch_2.pin_2, Reed_Switch_1.pin_1
  N29: Reed_Switch_0.pin_1, Reed_Switch_1.pin_2
  N30: R6.Pin_1, LED_5.C
